// Logisim project ddca pjtd2p2.circ as structural Verilog: 1 circuit, main circuit main
module main (
  input  P0,
  input  P1,
  input  P2,
  input  P3,
  input  K0,
  input  K1,
  input  K2,
  input  K3,
  output out_9,
  output out_10,
  output out_11,
  output out_12,
  output out_13
);

  wire C0_out, C1_out, C2_out, C3_out;

  xor C0 (C0_out, P0, K0);
  xor C1 (C1_out, P1, K1);
  xor C2 (C2_out, P2, K2);
  xor C3 (C3_out, P3, K3);
  xor D0 (out_9, C0_out, K0);
  xor D1 (out_10, C1_out, K1);
  xor D2 (out_11, C2_out, K2);
  xor D3 (out_13, C3_out, K3);
  Comparator #(.width(1)) comparator_1 (.a(P2), .b(out_11), .eq(out_12));  // open: gt, lt
endmodule
